# Fritzing sketch CyclaA (saved by Fritzing 0.3.12b)
breadboards: 1

parts:
  LED1 = Red LED - 5mm
  Arduino1 = Arduino
  LED5 = green LED - 5mm
  LED6 = yellow LED - 5mm
  LED7 = Blue LED - 5mm
  S1 = Pushbutton [package=THT]
  S2 = Pushbutton [package=THT]
  R1 = 220 Ω Resistor [package=THT]
  R1_2 = 220 Ω Resistor [package=THT]
  R1_3 = 220 Ω Resistor [package=THT]
  R1_4 = 220 Ω Resistor [package=THT]
  R3 = 10k Ω Resistor [package=THT]
  R3_2 = 10k Ω Resistor [package=THT]

nets:
  N1: LED1.cathode, Arduino1.GND, LED5.cathode, LED6.cathode, LED7.cathode, R3.Pin_1, R3_2.Pin_1
  N2: LED1.anode, R1.Pin_0
  N3: Arduino1.D12, R1_4.Pin_1
  N4: Arduino1.D11, R1_3.Pin_1
  N5: Arduino1.D10, R1_2.Pin_1
  N6: Arduino1.D9, R1.Pin_1
  N7: Arduino1.D3, S1.Pin_3, S1.Pin_4, R3_2.Pin_0
  N8: Arduino1.D2, S2.Pin_3, S2.Pin_4, R3.Pin_0
  N9: Arduino1.+5V, S1.Pin_1, S1.Pin_2, S2.Pin_1, S2.Pin_2
  N10: LED5.anode, R1_4.Pin_0
  N11: LED6.anode, R1_3.Pin_0
  N12: LED7.anode, R1_2.Pin_0
